# Fritzing sketch RGB led strip driver2 (saved by Fritzing 0.9.6b)
circuit board: 7.74446cm x 4.07528cm
breadboards: 1

parts:
  WeMos_D1_Mini1 = WeMos D1 Mini
  IC1 = ULN2003A [package="DIP16 [THT]"]
  Power_plug1 = Power plug
  JP1 = Header 4 [package=screwterminal-3.5mm-4_lock]
  JP2 = Header 4 [package=screwterminal-3.5mm-4_lock]
  Mini-360_DC-DC_Buck_converter = Mini-360 DC-DC Buck converter [package=THT]

nets:
  N1: WeMos_D1_Mini1.5V, Mini-360_DC-DC_Buck_converter.OUT+
  N2: WeMos_D1_Mini1.D2, IC1.In_3
  N3: WeMos_D1_Mini1.D3, IC1.In_2
  N4: WeMos_D1_Mini1.D4, IC1.In_1
  N5: WeMos_D1_Mini1.G, IC1.0V, Power_plug1.GND, Mini-360_DC-DC_Buck_converter.IN-, Mini-360_DC-DC_Buck_converter.OUT-
  N6: IC1.COM_-_Common, Power_plug1.VCC, JP1.4, JP2.4, Mini-360_DC-DC_Buck_converter.IN+
  N7: IC1.Out_3, JP1.3, JP2.3
  N8: IC1.Out_2, JP1.2, JP2.2
  N9: IC1.Out_1, JP1.1, JP2.1

notes:
  12V 5A DC Input
  Simple 5050 RGB led strip
  2 Connectors for both sides of the PCB
  12V to 5V DC Buck converter

custom parts:
  Mini-360 DC-DC Buck converter: Mini-360 DC-DC Buck converter. Tiny buck step down voltage converter, input voltage 4.75 to 23V output 1 to 17V adjustable. Available from ebay and the like.
